# Fritzing sketch shema (saved by Fritzing 0.9.3b)

parts:
  Часть1 = Arduino Uno (Rev3)
  J1 = Basic Servo
  J2 = Basic Servo
  J3 = Basic Servo
  J4 = Basic Servo
  J5 = Basic Servo
  Power_plug1 = Power plug
  J6 = Basic Servo
  Часть2 = Bluetooth HC-05 Macho
  R1 = Resistor [tolerance=±5% resistance=220 package=THT]
  R2 = Resistor [tolerance=±5% resistance=220 package=THT]

nets:
  N1: Часть1.D8, J4.pulse
  N2: Часть1.D9_PWM, J5.pulse
  N3: Часть1.D10_PWM/SS, J6.pulse
  N4: Часть1.D3_PWM, Часть2.TXD
  N5: Часть1.D4, R2.Pin_0
  N6: Часть1.D5_PWM, J1.pulse
  N7: Часть1.D6_PWM, J2.pulse
  N8: Часть1.D7, J3.pulse
  VCC: Часть1.5V, J1.vcc, J2.vcc, J3.vcc, J4.vcc, J5.vcc, Power_plug1.VCC, J6.vcc, Часть2.VCC
  GND: Часть1.GND, Часть2.GND
  GND_2: Power_plug1.GND, J6.gnd
  N9: Часть2.RXD, R1.Pin_1, R2.Pin_1

notes:
  mg966r
  s690
